// Logisim project 3-in-1-out-test.circ as structural Verilog: 1 circuit, main circuit main
module main (
  input  A,
  input  B,
  input  C,
  output OUT
);

  wire and_1_out, and_2_out, not_1_out, not_2_out;

  not not_1 (not_1_out, A);
  not not_2 (not_2_out, C);
  and and_1 (and_1_out, not_1_out, B, not_2_out);
  and and_2 (and_2_out, C, B);
  or or_1 (OUT, and_1_out, and_2_out);
endmodule
