// Logisim project tester.circ as structural Verilog: 1 circuit, main circuit main
module main (
  output halt
);

  wire clock_1_out;
  wire [9:0] counter_1_q;

  Counter #(.width(10), .max('h3ff)) counter_1 (
    .Q(counter_1_q), .carry(halt), .clk(clock_1_out));  // open: load, D, count, clr
  Clock clock_1 (.out(clock_1_out));
  // placeholder_main main_1: pin names not known
endmodule
