// Logisim project __TESTER_FILE.circ as structural Verilog: 1 circuit, main circuit main
module main (
  output out_1,
  output out_2,
  output out_3,
  output out_4,
  output out_5,
  output out_6,
  output out_7,
  output out_8,
  output halt
);

  wire clock_1_out;

  Counter #(.width(3), .max('h3ff)) counter_1 (
    .Q({out_3, out_2, out_1}), .carry(halt), .clk(clock_1_out));  // open: load, D, count, clr
  Clock clock_1 (.out(clock_1_out));
  // placeholder_main main_1: pin names not known; wires that end beside it: out_1, out_2, out_3, out_4, out_5, out_6, out_7
endmodule
