// Logisim project main.circ as structural Verilog: 1 circuit, main circuit main
module main (
  input  A,
  input  B,
  input  C,
  output out_4,
  output out_5
);

  _3_in_1_out_test_main main_1 (.A(A), .B(B), .C(C), .OUT(out_4));
  not not_1 (C, C);

  assign out_5 = C;
endmodule
