// Logisim project result.circ as structural Verilog: 1 circuit, main circuit main
module main (
  output out_1,
  output out_2,
  output out_3,
  output out_4,
  output out_5,
  output out_6,
  output out_7,
  output out_8,
  output out_9,
  output out_10,
  output out_11,
  output out_12,
  output out_13,
  output out_14,
  output out_15,
  output out_16,
  output out_17,
  output out_18,
  output out_19,
  output out_20,
  output halt
);

  wire clock_1_out;

  Counter #(.width(16), .max('h3ff)) counter_1 (
    .Q({out_16, out_15, out_14, out_13, out_12, out_11, out_10, out_9, out_8, out_7, out_6, out_5, out_4, out_3, out_2, out_1}),
    .carry(halt), .clk(clock_1_out));  // open: load, D, count, clr
  Clock clock_1 (.out(clock_1_out));
  // placeholder_main main_1: pin names not known; wires that end beside it: out_4, out_5, out_6, out_7, out_8, out_9, out_10, out_17, out_18, out_19, out_20
endmodule
